// Logisim project lab1.circ as structural Verilog: 3 circuits, main circuit 4 bit shift register
module _4_bit_shift_register (
  input  D3,
  input  D2,
  input  D1,
  input  D0,
  input  S0,
  input  S1,
  input  Left_shift_in,
  input  Right_shift_in,
  input  Clock,
  input  d_ff_enable,
  output Q3,
  output Q2,
  output Q1,
  output Q0
);

  wire multiplexer_1_out, multiplexer_2_out, multiplexer_3_out, multiplexer_4_out;

  Multiplexer #(.select(2), .enable("false")) multiplexer_1 (
    .in0(Q3), .in1(Q2), .in2(Right_shift_in), .in3(D3), .out(multiplexer_1_out), .sel({S1, S0}));
  D_Flip_Flop_part d_ff_1 (.clk(Clock), .D(multiplexer_1_out), .Q(Q3), .en(d_ff_enable));  // open: Qn, preset, reset
  Multiplexer #(.select(2), .enable("false")) multiplexer_2 (
    .in0(Q2), .in1(Q1), .in2(Q3), .in3(D2), .out(multiplexer_2_out), .sel({S1, S0}));
  D_Flip_Flop_part d_ff_2 (.clk(Clock), .D(multiplexer_2_out), .Q(Q2), .en(d_ff_enable));  // open: Qn, preset, reset
  Multiplexer #(.select(2), .enable("false")) multiplexer_3 (
    .in0(Q1), .in1(Q0), .in2(Q2), .in3(D1), .out(multiplexer_3_out), .sel({S1, S0}));
  D_Flip_Flop_part d_ff_3 (.clk(Clock), .D(multiplexer_3_out), .Q(Q1), .en(d_ff_enable));  // open: Qn, preset, reset
  Multiplexer #(.select(2), .enable("false")) multiplexer_4 (
    .in0(Q0), .in1(Left_shift_in), .in2(Q1), .in3(D0), .out(multiplexer_4_out), .sel({S1, S0}));
  D_Flip_Flop_part d_ff_4 (.clk(Clock), .D(multiplexer_4_out), .Q(Q0), .en(d_ff_enable));  // open: Qn, preset, reset

  // Notes on the sheet:
  //   4 bit shift register test circuit
endmodule

module D_Flip_Flop (
  input  Clock,
  input  D,
  input  Preset_1,
  input  Enable,
  input  Preset_0,
  output Q,
  output NOT_Q
);

  D_Flip_Flop_part d_ff_1 (.clk(Clock), .D(D), .Q(Q), .Qn(NOT_Q), .preset(Preset_1), .en(Enable), .reset(Preset_0));

  // Notes on the sheet:
  //   D FF Test Circuit
endmodule

module _4_1_Multiplexer (
  input  D0,
  input  D1,
  input  D2,
  input  D3,
  input  E,
  input  S1,
  input  S0,
  output Q
);

  Multiplexer #(.select(2)) multiplexer_1 (.in0(D0), .in1(D1), .in2(D2), .in3(D3), .out(Q), .sel({S1, S0}), .en(E));

  // Notes on the sheet:
  //   4-1 Multiplexer Test Circuit
endmodule
