// Logisim project lab2.circ as structural Verilog: 5 circuits, main circuit Registers
module Registers (
  input  in_1,
  input  in_2,
  input  [1:0] in_3,
  input  in_4,
  input  [7:0] in_5,
  input  in_6,
  input  in_7,
  output out_8,
  output [1:0] out_9,
  output [7:0] out_10
);

  wire undriven, undriven_2;

  Register #(.width(1)) register_1 (.D(in_1), .Q(out_8), .clk(in_2), .clr(undriven));  // open: en
  Register #(.width(2)) register_2 (.D(in_3), .Q(out_9), .clk(in_4), .clr(undriven_2));  // open: en
  Register register_3 (.D(in_5), .Q(out_10), .clk(in_6), .clr(in_7));  // open: en

  // Notes on the sheet:
  //   One bit
  //   Two bit
  //   8 bit
endmodule

module Tri_State_Buffers (
  input  in_1,
  input  in_2,
  input  [1:0] in_3,
  input  in_4,
  input  [7:0] in_5,
  input  in_6,
  output out_7,
  output [1:0] out_8,
  output [7:0] out_9
);

  assign out_7 = in_2 ? in_1 : 1'bz;  // Controlled_Buffer controlled_buffer_1
  assign out_8 = in_4 ? in_3 : 2'bz;  // Controlled_Buffer controlled_buffer_2
  assign out_9 = in_6 ? in_5 : 8'bz;  // Controlled_Buffer controlled_buffer_3

  // Notes on the sheet:
  //   2-bit
  //   8-bit
  //   1 bit
endmodule

module Decoders (
  input  Enable,
  input  in_2,
  input  Enable_2,
  input  [1:0] in_4,
  input  Enable_3,
  input  [2:0] in_6,
  output out_7,
  output out_8,
  output out_9,
  output out_10,
  output out_11,
  output out_12,
  output out_13,
  output out_14,
  output out_15,
  output out_16,
  output out_17,
  output out_18,
  output out_19,
  output out_20
);

  Decoder decoder_1 (.out0(out_7), .out1(out_8), .sel(in_2), .en(Enable));
  Decoder #(.select(2)) decoder_2 (
    .out0(out_9), .out1(out_10), .out2(out_11), .out3(out_12), .sel(in_4), .en(Enable_2));
  Decoder #(.select(3)) decoder_3 (
    .out0(out_13), .out1(out_14), .out2(out_15), .out3(out_16), .out4(out_17), .out5(out_18), .out6(out_19),
    .out7(out_20), .sel(in_6), .en(Enable_3));

  // Notes on the sheet:
  //   1-2 decoder
  //   2-4 decoder
  //   3-8 decoder
endmodule

module _1_Bit_CPU (
  input  ACCout,
  input  Bin,
  input  Cin,
  input  EXTin,
  input  Bout,
  input  Cout,
  input  TMPin,
  input  ACCin,
  input  IRin,
  input  EXTOut,
  input  TMPout,
  input  ALUout,
  input  EN,
  output out_14
);

  wire ACC_q, and_1_out, B_q, C_q, IR_q, multiplexer_1_out, TMP_q, xor_1_out;

  assign out_14 = EXTOut ? EXTin : 1'bz;  // Controlled_Buffer controlled_buffer_1
  Register #(.width(1)) TMP (.D(out_14), .Q(TMP_q), .clk(TMPin));  // open: en, clr
  assign out_14 = TMPout ? TMP_q : 1'bz;  // Controlled_Buffer controlled_buffer_2
  xor xor_1 (xor_1_out, TMP_q, ACC_q);
  and and_1 (and_1_out, ACC_q, TMP_q);
  Register #(.width(1)) ACC (.D(out_14), .Q(ACC_q), .clk(ACCin));  // open: en, clr
  assign out_14 = ACCout ? ACC_q : 1'bz;  // Controlled_Buffer controlled_buffer_3
  Multiplexer multiplexer_1 (.in0(xor_1_out), .in1(and_1_out), .out(multiplexer_1_out), .sel(IR_q), .en(EN));
  Register #(.width(1)) IR (.D(out_14), .Q(IR_q), .clk(IRin));  // open: en, clr
  assign out_14 = ALUout ? multiplexer_1_out : 1'bz;  // Controlled_Buffer controlled_buffer_4
  Register #(.width(1)) B (.D(out_14), .Q(B_q), .clk(Bin));  // open: en, clr
  assign out_14 = Bout ? B_q : 1'bz;  // Controlled_Buffer controlled_buffer_5
  Register #(.width(1)) C (.D(out_14), .Q(C_q), .clk(Cin));  // open: en, clr
  assign out_14 = Cout ? C_q : 1'bz;  // Controlled_Buffer controlled_buffer_6

  // Notes on the sheet:
  //   1-Bit CPU
endmodule

module _2_Bit_CPU (
  input  ACCout,
  input  Bin,
  input  Cin,
  input  [1:0] EXTin,
  input  Bout,
  input  Cout,
  input  TMPin,
  input  ACCin,
  input  IRin,
  input  EXTOut,
  input  TMPout,
  input  ALUout,
  input  EN,
  output [1:0] out_14
);

  wire [1:0] ACC_q, and_1_out, B_q, C_q, IR_q, multiplexer_1_out, not_1_out, or_1_out, TMP_q, xor_1_out;

  assign out_14 = EXTOut ? EXTin : 2'bz;  // Controlled_Buffer controlled_buffer_1
  Register #(.width(2)) TMP (.D(out_14), .Q(TMP_q), .clk(TMPin));  // open: en, clr
  assign out_14 = TMPout ? TMP_q : 2'bz;  // Controlled_Buffer controlled_buffer_2
  assign xor_1_out = TMP_q ^ ACC_q;  // XOR_Gate xor_1, 2 bits wide
  assign and_1_out = ACC_q & TMP_q;  // AND_Gate and_1, 2 bits wide
  assign or_1_out = ACC_q | TMP_q;  // OR_Gate or_1, 2 bits wide
  assign not_1_out = ~ACC_q;  // NOT_Gate not_1, 2 bits wide
  Register #(.width(2)) ACC (.D(out_14), .Q(ACC_q), .clk(ACCin));  // open: en, clr
  assign out_14 = ACCout ? ACC_q : 2'bz;  // Controlled_Buffer controlled_buffer_3
  Multiplexer #(.select(2), .width(2)) multiplexer_1 (
    .in0(xor_1_out), .in1(and_1_out), .in2(not_1_out), .in3(or_1_out), .out(multiplexer_1_out), .sel(IR_q),
    .en(EN));
  Register #(.width(2)) IR (.D(out_14), .Q(IR_q), .clk(IRin));  // open: en, clr
  assign out_14 = ALUout ? multiplexer_1_out : 2'bz;  // Controlled_Buffer controlled_buffer_4
  Register #(.width(2)) B (.D(out_14), .Q(B_q), .clk(Bin));  // open: en, clr
  assign out_14 = Bout ? B_q : 2'bz;  // Controlled_Buffer controlled_buffer_5
  Register #(.width(2)) C (.D(out_14), .Q(C_q), .clk(Cin));  // open: en, clr
  assign out_14 = Cout ? C_q : 2'bz;  // Controlled_Buffer controlled_buffer_6

  // Notes on the sheet:
  //   2-Bit CPU
endmodule
