// Logisim project lab3.circ as structural Verilog: 2 circuits, main circuit 8-bit ram
module _8_bit_ram (
  input  [7:0] EXT_Input,
  input  MAR_in,
  input  MEM_io,
  input  MEM_enable,
  input  MEM_clk,
  output [7:0] mem_out,
  output [7:0] address
);

  wire not_1_out;
  wire [7:0] controlled_buffer_1_out;

  Register register_1 (.D(EXT_Input), .Q(address), .clk(MAR_in));  // open: en, clr
  assign controlled_buffer_1_out = MEM_io ? EXT_Input : 8'bz;  // Controlled_Buffer controlled_buffer_1
  not not_1 (not_1_out, MEM_io);
  RAM ram_1 (
    .addr(address), .data(controlled_buffer_1_out), .sel(MEM_enable), .clk(MEM_clk), .ld(not_1_out));  // open: clr
  assign mem_out = not_1_out ? controlled_buffer_1_out : 8'bz;  // Controlled_Buffer controlled_buffer_2

  // Notes on the sheet:
  //   1 store, 0 load
endmodule

module _8_bit_cpu (
  input  [7:0] EXT_in,
  input  EXT_out,
  input  MEM_out,
  input  PC_in,
  input  PC_out,
  input  MAR_out,
  input  MAR_in,
  input  MEM_en,
  input  MEM_in,
  input  PC__1_out,
  input  PC___1_in,
  input  C_in,
  input  C_out,
  input  IR_in,
  input  B_in,
  input  B_out,
  input  ALU_out,
  input  ACC_in,
  input  ACC_out,
  input  ALU_en,
  input  TMP_in,
  input  TMP_out
);

  wire not_1_out;
  wire [1:0] bitselector_1_out;
  wire [7:0] ACC_q, adder_1_out, and_1_out, B_q, C_q, controlled_buffer_1_out, controlled_buffer_5_out,
       controlled_buffer_6_out, IR_q, MAR_q, multiplexer_1_out, not_2_out, or_1_out, PC___1_q, PC_q, TMP_q,
       xor_1_out;

  Register PC (.D(controlled_buffer_1_out), .Q(PC_q), .clk(PC_in));  // open: en, clr
  Adder adder_1 (.a(PC_q), .b(8'h1), .out(adder_1_out));  // open: cin, cout
  Register PC___1 (.D(adder_1_out), .Q(PC___1_q), .clk(PC___1_in));  // open: en, clr
  Register IR (.D(controlled_buffer_1_out), .Q(IR_q), .clk(IR_in));  // open: en, clr
  assign controlled_buffer_1_out = PC_out ? PC_q : 8'bz;  // Controlled_Buffer controlled_buffer_1
  assign controlled_buffer_1_out = PC__1_out ? PC___1_q : 8'bz;  // Controlled_Buffer controlled_buffer_2
  BitSelector #(.group(2)) bitselector_1 (.in(IR_q), .out(bitselector_1_out), .sel(2'b00));
  assign controlled_buffer_1_out = EXT_out ? EXT_in : 8'bz;  // Controlled_Buffer controlled_buffer_3
  Register MAR (.D(controlled_buffer_1_out), .Q(MAR_q), .clk(MAR_in));  // open: en, clr
  Register C (.D(controlled_buffer_1_out), .Q(C_q), .clk(C_in));  // open: en, clr
  Register B (.D(controlled_buffer_1_out), .Q(B_q), .clk(B_in));  // open: en, clr
  Register ACC (.D(controlled_buffer_1_out), .Q(ACC_q), .clk(ACC_in));  // open: en, clr
  Register TMP (.D(controlled_buffer_1_out), .Q(TMP_q), .clk(TMP_in));  // open: en, clr
  assign controlled_buffer_1_out = MEM_out ? controlled_buffer_6_out : 8'bz;  // Controlled_Buffer controlled_buffer_4
  assign controlled_buffer_5_out = MAR_out ? MAR_q : 8'bz;  // Controlled_Buffer controlled_buffer_5
  assign controlled_buffer_6_out = MEM_in ? controlled_buffer_1_out : 8'bz;  // Controlled_Buffer controlled_buffer_6
  assign controlled_buffer_1_out = C_out ? C_q : 8'bz;  // Controlled_Buffer controlled_buffer_7
  assign controlled_buffer_1_out = B_out ? B_q : 8'bz;  // Controlled_Buffer controlled_buffer_8
  assign controlled_buffer_1_out = ACC_out ? ACC_q : 8'bz;  // Controlled_Buffer controlled_buffer_9
  assign controlled_buffer_1_out = TMP_out ? TMP_q : 8'bz;  // Controlled_Buffer controlled_buffer_10
  not not_1 (not_1_out, MEM_in);
  assign xor_1_out = TMP_q ^ ACC_q;  // XOR_Gate xor_1, 8 bits wide
  assign and_1_out = TMP_q & ACC_q;  // AND_Gate and_1, 8 bits wide
  assign or_1_out = TMP_q | ACC_q;  // OR_Gate or_1, 8 bits wide
  assign not_2_out = ~ACC_q;  // NOT_Gate not_2, 8 bits wide
  RAM ram_1 (
    .addr(controlled_buffer_5_out), .data(controlled_buffer_6_out), .sel(MEM_en), .clk(MEM_en), .ld(not_1_out));  // open: clr
  assign controlled_buffer_1_out = ALU_out ? multiplexer_1_out : 8'bz;  // Controlled_Buffer controlled_buffer_11
  Multiplexer #(.select(2), .width(8)) multiplexer_1 (
    .in0(xor_1_out), .in1(and_1_out), .in2(not_2_out), .in3(or_1_out), .out(multiplexer_1_out),
    .sel(bitselector_1_out), .en(ALU_en));

  // Notes on the sheet:
  //   Data Bus
endmodule
